# Fritzing sketch HomeWeatherStation (saved by Fritzing 0.9.3b)
breadboards: 1

parts:
  nodeMCU_ESP12-E = NodeMCU V1.0
  Squix2 = OLED 0.96" 128x64 I2C SSD1306
  DHT22 = Humidity and Temperature Sensor RHT03 [part_number="TEMP/HUM SENSOR"]
  part = Resistor [tolerance=±5% resistance=10k package=THT]

nets:
  N1: nodeMCU_ESP12-E.D1, Squix2.SCA
  N2: nodeMCU_ESP12-E.D2, Squix2.SCL
  N3: nodeMCU_ESP12-E.D3, DHT22.Data-signal, part.Pin_1
  VCC: nodeMCU_ESP12-E.3V3, Squix2.VCC, DHT22.Vcc
  GND: nodeMCU_ESP12-E.GND, Squix2.GND, DHT22.GND_2

custom parts:
  NodeMCU V1.0: ESP8266 based NodeMCU
